# Fritzing sketch dj-scm-hw (saved by Fritzing 0.9.3b)

parts:
  Part1 = Adafruit Circuit Playground Express [part_number="Adafruit #3333"]
  NEOPIXEL1 = Neopixel Strip -- Black (30/m) [part_number=1376]
  NEOPIXEL2 = Neopixel Strip -- Black (30/m) [part_number=1376]

nets:
  GND: Part1.GND, NEOPIXEL1.GND, NEOPIXEL2.GND
  +5V: Part1.VOUT, NEOPIXEL1.+5V, NEOPIXEL2.+5V

custom parts:
  Adafruit Circuit Playground Express: Circuit Playground Express is the next step towards a perfect introduction to electronics and programming. We've taken the original Circuit Playground Classic and made it even better! Not only did we pack even more sensors in, we also made it even easier to program. You can now start your journey with Microsoft MakeCode block-based or Javascript programming. Then, you can use the same board to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
  Neopixel Strip -- Black (30/m): These NeoPixel strips have 30 digitally-addressable pixel LEDs per meter and are very affordable and are only 12.5 mm wide, 10 mm if you remove the strip from the casing.
